# Fritzing sketch partdesign (saved by Fritzing 0.9.10b)

parts:
  Mod1 = Amica NodeMCU DEVKIT 1.0
  HC-SR04_Sensor_1 = HC-SR04 Ultrasonic Distance Sensor
  J1 = Basic Servo
  J2 = Basic Servo
  LCD1 = LCD screen
  LCM1602_IIC2 = LCM1602 IIC [part_number="LCM1602 IIC" chip_label="LCM1602 IIC" package="DIP (Dual Inline) [THT]"]
  Load_Cell3 = Load Cell - Red/white/black/green
  Part3 = HX711 Weighing Sensor Module

nets:
  GND: Mod1.pin2, Mod1.pin_25, Mod1.pin_29, HC-SR04_Sensor_1.GND, J1.gnd, J2.gnd, LCM1602_IIC2.GND, Part3.GND
  N1: Mod1.pin5, J1.pulse
  N2: Mod1.pin6, Part3.CK/TX
  N3: Mod1.pin7, Part3.DO/RX
  N4: Mod1.pin_11, LCM1602_IIC2.SDA
  N5: Mod1.pin_12, LCM1602_IIC2.SCL
  N6: Mod1.pin_13, HC-SR04_Sensor_1.TRIG
  N7: Mod1.pin_14, HC-SR04_Sensor_1.ECHO
  VCC: Mod1.pin_30, HC-SR04_Sensor_1.VCC, J1.vcc, J2.vcc, LCM1602_IIC2.VCC, Part3.VCC
  VSS: LCD1.VSS, LCM1602_IIC2.VSS
  VDD: LCD1.VDD, LCM1602_IIC2.VDD
  N8: LCD1.V0, LCM1602_IIC2.V0
  N9: LCD1.RS, LCM1602_IIC2.RS
  N10: LCD1.R/W, LCM1602_IIC2.RW
  N11: LCD1.E, LCM1602_IIC2.E
  N12: LCD1.DB0, LCM1602_IIC2.D0
  N13: LCD1.DB1, LCM1602_IIC2.D1
  N14: LCD1.DB2, LCM1602_IIC2.D2
  N15: LCD1.DB3, LCM1602_IIC2.D3
  N16: LCD1.DB4, LCM1602_IIC2.D4
  N17: LCD1.DB5, LCM1602_IIC2.D5
  N18: LCD1.DB6, LCM1602_IIC2.D6
  N19: LCD1.DB7, LCM1602_IIC2.D7
  N20: LCD1.LED+, LCM1602_IIC2.A
  N21: LCD1.LED-, LCM1602_IIC2.K
  N22: Load_Cell3.wire1, Part3.E+
  N23: Load_Cell3.wire2, Part3.A+
  N24: Load_Cell3.wire3, Part3.E-
  N25: Load_Cell3.wire4, Part3.A-

custom parts:
  LCM1602 IIC: I2C-Module to use a 1602 or 2004 LCD on with the wire.h libory Serial LCD Modul
  Load Cell - Red/white/black/green: A rectangle load cell/weighting pressure Sensor with four wires - Red, white, black, green. Normally corresponding with E+, E-, A+, A- respectively.
  HX711 Weighing Sensor Module: HX711 is a precision 24-bit analog-to-digital converter (ADC) designed for weigh scales and industrial control applications to interface directly with a bridge sensor.
